# Fritzing sketch minitag (saved by Fritzing 1.0.4)
circuit board: 8.55684cm x 5.23886cm
breadboards: 1

parts:
  part = Humidity and Temperature Sensor RHT03
  part_2 = Toggle Switch [package=THT]
  part_3 = Battery [internal_resistance=0.1Ω]
  wemos = WeMos D1 Mini
  part_4 = Toggle Switch [package=THT]
  part_5 = Toggle Switch [package=THT]
  rf_1 = Toggle Switch [package=THT]
  part_6 = Resistor [tolerance=±5% power=0.25W resistance=220 package=THT]
  R2 = Resistor [tolerance=±5% power=0.25W resistance=220 package=THT]
  Q1 = NPN-Transistor [package="TO92 [THT]"]
  part_7 = LED - 5mm [color="Red (633nm)" current=0.030A package="5 mm [THT]"]
  S2 = Pushbutton [package="[THT]"]  # not connected
  S3 = Pushbutton [package="[THT]"]  # not connected

nets:
  N1: part.Vcc, part_2.L1, wemos.G, Q1.C
  N2: part.Data-signal, part_2.L2, wemos.5V, Q1.B
  N3: part.GND_1, wemos.D1
  N4: part.GND_2, wemos.D2, rf_1.COM
  N5: part_2.COM, part_3.+, rf_1.L1
  N6: wemos.D3, Q1.E
  N7: wemos.D4, part_7.cathode
  N8: wemos.D5, part_4.COM
  N9: wemos.D6, part_5.L2, R2.Pin_0, R2.Pin_1
  N10: wemos.D8, part_4.L2
  N11: part_4.L1, part_6.Pin_0, part_6.Pin_1

notes:
  @baris_drmss
